# Fritzing sketch MeterReader (saved by Fritzing 0.9.2b)
breadboards: 1

parts:
  Part1 = Arduino Uno (Rev3)
  U1 = ESP8266 WiFi Module [part_number=ESP8266]
  R1 = Resistor [tolerance=±5% resistance=220 package=THT]
  ZS-042_RTC1 = ZS-042 RTC Module
  Q2 = 2N7000 FET N-Channel [part_number=2N7000 package=TO92]
  IR1 = TSOP312.., 314.. [package=THT]

nets:
  N1: Part1.A4/SDA, ZS-042_RTC1.SDA
  N2: Part1.A5/SCL, ZS-042_RTC1.SCL
  N3: Part1.D8, U1.TXD
  N4: Part1.D9_PWM, R1.Pin_1, Q2.drain
  N5: Part1.D2, IR1.Data
  N6: Part1.D3_PWM, ZS-042_RTC1.SQW
  N7: Part1.D7, U1.RST
  3V3: Part1.3V3, U1.VCC, U1.CH_PD, R1.Pin_0, Q2.gate
  5V: Part1.5V, ZS-042_RTC1.VCC, IR1.Vs
  GND: Part1.GND, U1.GND, ZS-042_RTC1.GND, IR1.GND
  N8: U1.RXD, Q2.source

custom parts:
  ESP8266 WiFi Module: Generic WiFi Module based on the ESP8266 with onboard PCB antenna and UART communications
  2N7000 FET N-Channel: A 2N7000 MOSFET N-Channel Transistor
